// Logisim project 4BitCPU.circ as structural Verilog: 5 circuits, main circuit main
module main (
  input  [3:0] in_1,
  input  [3:0] in_2
);

  wire clock_1_out, decoder_1_out0, decoder_1_out1, decoder_1_out2, decoder_1_out3, decoder_1_out4,
       decoder_1_out5, decoder_1_out6, decoder_1_out7, decoder_1_out8, not_1_out, not_2_out, or_1_out,
       or_2_out, or_3_out, or_4_out, or_5_out;
  wire [3:0] A_out_6, alu_1_out_7, B_out_6, controlled_buffer_1_out, ram_1_dout;

  Clock clock_1 (.out(clock_1_out));
  not not_1 (not_1_out, clock_1_out);
  not not_2 (not_2_out, clock_1_out);
  Decoder #(.select(4)) decoder_1 (
    .out0(decoder_1_out0), .out1(decoder_1_out1), .out2(decoder_1_out2), .out3(decoder_1_out3),
    .out4(decoder_1_out4), .out5(decoder_1_out5), .out6(decoder_1_out6), .out7(decoder_1_out7),
    .out8(decoder_1_out8), .sel(in_2));  // open: out9, out10, out11, out12, out13, out14, out15, en
  or or_1 (or_1_out, decoder_1_out8, decoder_1_out7, decoder_1_out6, decoder_1_out5);
  or or_2 (or_2_out, or_1_out, decoder_1_out2);
  reg4 A (
    .DataIn(alu_1_out_7), .RegIn(or_2_out), .RegOut(decoder_1_out1), .Clock(not_1_out), .out_6(A_out_6));  // open: out_5
  reg4 B (
    .DataIn(alu_1_out_7), .RegIn(decoder_1_out4), .RegOut(decoder_1_out3), .Clock(not_2_out), .out_6(B_out_6));  // open: out_5
  or or_3 (or_3_out, decoder_1_out1, decoder_1_out3);
  or or_4 (or_4_out, decoder_1_out2, decoder_1_out4);
  assign controlled_buffer_1_out = decoder_1_out1 ? A_out_6 : 4'bz;  // Controlled_Buffer controlled_buffer_1
  assign controlled_buffer_1_out = decoder_1_out3 ? B_out_6 : 4'bz;  // Controlled_Buffer controlled_buffer_2
  RAM #(.addrWidth(4), .dataWidth(4)) ram_1 (
    .addr(in_1), .we(or_3_out), .oe(or_4_out), .clk(clock_1_out), .din(controlled_buffer_1_out),
    .dout(ram_1_dout));
  ALU alu_1 (
    .A(A_out_6), .B(B_out_6), .CLR(decoder_1_out5), .ADD(decoder_1_out6), .SUB(decoder_1_out7),
    .CMP(decoder_1_out8), .out_7(alu_1_out_7));
  or or_5 (or_5_out, decoder_1_out4, decoder_1_out2);
  assign alu_1_out_7 = or_5_out ? ram_1_dout : 4'bz;  // Controlled_Buffer controlled_buffer_3
  Hex_Digit_Display BusVal (.value(alu_1_out_7));  // open: dp
  Hex_Digit_Display AVal (.value(A_out_6));  // open: dp
  Hex_Digit_Display BVal (.value(B_out_6));  // open: dp

  // Notes on the sheet:
  //   STORE A - LOAD A STORE B - LOAD B
  //   BVal
endmodule

module reg4 (
  input  [3:0] DataIn,
  input  RegIn,
  input  RegOut,
  input  Clock,
  output [3:0] out_5,
  output [3:0] out_6
);

  wire and_1_out, and_2_out;

  and and_1 (and_1_out, RegIn, Clock);
  and and_2 (and_2_out, Clock, RegOut);
  D_Flip_Flop d_ff_1 (.D(DataIn[0]), .clk(and_1_out), .Q(out_6[0]));  // open: Qn, preset, reset
  D_Flip_Flop d_ff_2 (.D(DataIn[1]), .clk(and_1_out), .Q(out_6[1]));  // open: Qn, preset, reset
  D_Flip_Flop d_ff_3 (.D(DataIn[2]), .clk(and_1_out), .Q(out_6[2]));  // open: Qn, preset, reset
  D_Flip_Flop d_ff_4 (.D(DataIn[3]), .clk(and_1_out), .Q(out_6[3]));  // open: Qn, preset, reset
  assign out_5 = and_2_out ? out_6 : 4'bz;  // Controlled_Buffer controlled_buffer_1
endmodule

module ALU (
  input  [3:0] A,
  input  [3:0] B,
  input  CLR,
  input  ADD,
  input  SUB,
  input  CMP,
  output [3:0] out_7
);

  wire [1:0] decoder2_1_out_5;
  wire [3:0] adder_1_out, cmp4_1_out_4, subtractor_1_out;

  Hex_Digit_Display hex_digit_display_1 (.value(A));  // open: dp
  Hex_Digit_Display hex_digit_display_2 (.value(B));  // open: dp
  Adder #(.width(4)) adder_1 (.a(A), .b(B), .out(adder_1_out));  // open: cin, cout
  Subtractor #(.width(4)) subtractor_1 (.a(A), .b(B), .out(subtractor_1_out));  // open: bin, bout
  Hex_Digit_Display hex_digit_display_3 (.value(adder_1_out));  // open: dp
  Decoder2 decoder2_1 (.in_1(CLR), .in_2(ADD), .in_3(SUB), .in_4(CMP), .out_5(decoder2_1_out_5));
  CMP4 cmp4_1 (.in_1(A), .in_2(B), .out_4(cmp4_1_out_4));  // open: in_3
  Hex_Digit_Display hex_digit_display_4 (.value(subtractor_1_out));  // open: dp
  Multiplexer #(.select(2), .width(4)) multiplexer_1 (
    .in1(adder_1_out), .in2(subtractor_1_out), .in3(cmp4_1_out_4), .out(out_7), .sel(decoder2_1_out_5));  // open: in0
  Hex_Digit_Display hex_digit_display_5 (.value(out_7));  // open: dp

  // Notes on the sheet:
  //   CMP
endmodule

module CMP4 (
  input  [3:0] in_1,
  input  [3:0] in_2,
  input  in_3,
  output [3:0] out_4
);

  Comparator #(.mode("unsigned"), .width(4)) comparator_1 (
    .a(in_1), .b(in_2), .gt(out_4[0]), .eq(out_4[1]), .lt(out_4[2]));

  assign out_4[3] = in_3;
endmodule

module Decoder2 (
  input  in_1,
  input  in_2,
  input  in_3,
  input  in_4,
  output [1:0] out_5
);

  or or_1 (out_5[0], in_2, in_4);
  or or_2 (out_5[1], in_3, in_4);

  // Notes on the sheet:
  //   00 01 10 11
endmodule
